# Fritzing sketch ConnectionDiagram (saved by Fritzing 0.9.3b)

parts:
  S2 = Round Pushbutton
  S3 = Round Pushbutton
  S4 = Round Pushbutton
  10K = Resistor [tolerance=±5% resistance=220 package=THT]
  Part1 = Adafruit Feather nRF52840 [part_number=4062]
  S5 = Round Pushbutton
  J3 = Piezo Speaker
  10K_2 = Resistor [tolerance=±5% resistance=220 package=THT]  # not connected
  Q2 = NPN-Transistor [package="TO92 [THT]"]

nets:
  N1: S2.leg0, Part1.A4
  N2: S3.leg0, Part1.A2
  N3: S3.leg1, S4.leg1
  N4: S4.leg0, Part1.A3
  N5: 10K.Pin_0, Q2.B
  N6: 10K.Pin_1, Part1.D13
  N7: Part1.A1, S5.leg0
  N8: J3.pin1, Q2.C

notes:
  Feather Board
  Pin A4 - morse key 1
  Pin A3 - morse key 2
  Pin A2 - morse key 3
  Pin A1 - mode key
  Pin D13 - buzzer
  Key 1
  Buzzer
  Key 2
  Key 3
  Mode key

custom parts:
  Adafruit Feather nRF52840: The Adafruit Feather nRF52840 Express is our take on an 'all-in-one' Arduino-compatible + Bluetooth Low Energy with built in USB plus battery charging, 1 MB of FLASH and 256KB of SRAM. With native USB it's even ready to join the CircuitPython party. For this chip, we've added Arduino IDE support - you can program the nRF52840 chip directly to take full advantage of the Cortex-M4 processor, and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
